# Fritzing sketch hardwareontwerp (saved by Fritzing 0.9.3b)
circuit board: 13.7347cm x 7.39106cm
breadboards: 1

parts:
  Onderdeel2 = Arduino Ethernet Shield (Rev3)
  S1 = Pushbutton [package="[THT]"]
  R1 = Resistor [tolerance=±5% resistance=10k package=THT]
  R2 = Resistor [tolerance=±5% resistance=220 package=THT]
  R3 = Resistor [tolerance=±5% resistance=220 package=THT]
  R4 = Resistor [tolerance=±5% resistance=220 package=THT]
  LED1 = LED - 5mm [color="Red (633nm)" package="5 mm [THT]"]
  LED2 = LED - 5mm [color="Green (555nm)" package="5 mm [THT]"]
  LED3 = LED - 5mm [color="Yellow (595nm)" package="5 mm [THT]"]
  R5 = Resistor [tolerance=±5% resistance=220 package=THT]
  R6 = Resistor [tolerance=±5% resistance=10k package=THT]
  R7 = Photocell (LDR) [package=THT]
  DS1 = DS18B20 1-Wire Temperature Sensor [part_number=DS18B20]

nets (from the breadboard view):
  N1: Onderdeel2.D8, LED1.anode
  GND: Onderdeel2.GND, S1.Pin_1, S1.Pin_2, R2.Pin_1, R3.Pin_1, R4.Pin_1, R7.pin_1, DS1.GND
  N2: Onderdeel2.A1, R6.Pin_0, R7.pin_0
  N3: Onderdeel2.D2, S1.Pin_3, S1.Pin_4, R1.Pin_1
  N4: Onderdeel2.SDCS, R5.Pin_0, DS1.DQ
  N5: Onderdeel2.PWM_D6, LED3.anode
  N6: Onderdeel2.D7, LED2.anode
  5V: Onderdeel2.5V, R1.Pin_0, R5.Pin_1, R6.Pin_1, DS1.VDD
  N7: R2.Pin_0, LED1.cathode
  N8: R3.Pin_0, LED2.cathode
  N9: R4.Pin_0, LED3.cathode
